# Fritzing sketch mkr-ds18b20-temp-sensor-circuit-diagram (saved by Fritzing 0.9.3b)
breadboards: 1

parts:
  DS1 = DS18B20 1-Wire Temperature Sensor [part_number=DS18B20]
  R1 = Resistor [tolerance=±5% resistance=4.7k package=THT]
  Part1 = Arduino MKR WiFi 1010

nets:
  GND: DS1.GND, Part1.GND
  N1: DS1.DQ, R1.Pin_0, Part1.D7
  VDD: DS1.VDD, R1.Pin_1, Part1.VCC

custom parts:
  Arduino MKR WiFi 1010: This is the newest version of the MKR 1000 WIFI, but with an ESP32 module on board made by U-BLOX.
