# Fritzing sketch uno-ds18b20-temp-sensor-circuit-diagram (saved by Fritzing 0.9.3b)
breadboards: 1

parts:
  DS1 = DS18B20 1-Wire Temperature Sensor [part_number=DS18B20]
  R1 = Resistor [tolerance=±5% resistance=4.7k package=THT]
  Part2 = Arduino Uno (Rev3)

nets:
  GND: DS1.GND, Part2.GND
  N1: DS1.DQ, R1.Pin_0, Part2.D7
  VDD: DS1.VDD, R1.Pin_1, Part2.5V
