# Fritzing sketch esp32-ds18b20-temp-sensor-circuit-diagram (saved by Fritzing 0.9.3b)
breadboards: 1

parts:
  DS1 = DS18B20 1-Wire Temperature Sensor [part_number=DS18B20]
  R1 = Resistor [tolerance=±5% resistance=4.7k package=THT]
  U1 = Wemos Lolin D32

nets:
  N1: DS1.GND, U1.pin_22, U1.pin_37
  N2: DS1.DQ, R1.Pin_0, U1.pin_25
  N3: DS1.VDD, R1.Pin_1, U1.pin_0

custom parts:
  Wemos Lolin D32: Based on Peter Van Epp (vanepp in forums) Wemos Lolin 32 wifi and blue tooth board based on the ESP-32 cpu
